// Logisim project advent.circ as structural Verilog: 2 circuits, main circuit main
module main (
);

  wire button_1_out, clk0, clk1, clk2, clock_4_out, comparator_6_eq, nor_1_out, not_3_out, odd_parity_1_out,
       Q0, rst, rst_out, run;
  wire [1:0] N_out, shift_register_1_q1;
  wire [2:0] MUX2, U_out;
  wire [4:0] Keypad, MUX1, not_2_out;
  wire [7:0] adder_1_out, AdventText_data, counter_1_q, counter_2_q, D, De, demultiplexer_1_out0,
       demultiplexer_1_out1, demultiplexer_1_out2, demultiplexer_1_out3, demultiplexer_1_out4,
       demultiplexer_1_out5, demultiplexer_1_out6, demultiplexer_1_out7, demultiplexer_1_out8,
       demultiplexer_1_out9, demultiplexer_1_out10, demultiplexer_1_out11, demultiplexer_1_out12,
       demultiplexer_1_out13, demultiplexer_1_out14, demultiplexer_1_out15, demultiplexer_1_out16,
       demultiplexer_1_out17, demultiplexer_1_out18, demultiplexer_1_out19, demultiplexer_1_out20,
       demultiplexer_1_out21, demultiplexer_1_out22, demultiplexer_1_out23, demultiplexer_1_out24,
       demultiplexer_1_out25, demultiplexer_1_out26, demultiplexer_1_out27, demultiplexer_1_out28,
       demultiplexer_1_out29, demultiplexer_1_out30, demultiplexer_1_out31, demultiplexer_2_out0,
       demultiplexer_2_out1, demultiplexer_2_out2, demultiplexer_2_out3, demultiplexer_2_out4,
       demultiplexer_2_out5, demultiplexer_2_out6, demultiplexer_2_out7, demultiplexer_2_out8,
       demultiplexer_2_out9, demultiplexer_2_out10, demultiplexer_2_out11, demultiplexer_2_out12,
       demultiplexer_2_out13, demultiplexer_2_out14, demultiplexer_2_out15, demultiplexer_2_out16,
       demultiplexer_2_out17, demultiplexer_2_out18, demultiplexer_2_out19, demultiplexer_2_out20,
       demultiplexer_2_out21, demultiplexer_2_out22, demultiplexer_2_out23, demultiplexer_2_out24,
       demultiplexer_2_out25, demultiplexer_2_out26, demultiplexer_2_out27, demultiplexer_2_out28,
       demultiplexer_2_out29, demultiplexer_2_out30, demultiplexer_2_out31, demultiplexer_3_out0,
       demultiplexer_3_out1, demultiplexer_3_out2, demultiplexer_3_out3, demultiplexer_4_out0,
       demultiplexer_4_out1, demultiplexer_4_out2, demultiplexer_4_out3, demultiplexer_4_out4,
       demultiplexer_4_out5, demultiplexer_4_out6, demultiplexer_4_out7, demultiplexer_4_out8,
       demultiplexer_4_out9, demultiplexer_4_out10, demultiplexer_4_out11, demultiplexer_4_out12,
       demultiplexer_4_out13, demultiplexer_4_out14, demultiplexer_4_out15, demultiplexer_4_out16,
       demultiplexer_4_out17, demultiplexer_4_out18, demultiplexer_4_out19, demultiplexer_4_out20,
       demultiplexer_4_out21, demultiplexer_4_out22, demultiplexer_4_out23, demultiplexer_4_out24,
       demultiplexer_4_out25, demultiplexer_4_out26, demultiplexer_4_out27, demultiplexer_4_out28,
       demultiplexer_4_out29, demultiplexer_4_out30, demultiplexer_4_out31, demultiplexer_5_out0,
       demultiplexer_5_out1, demultiplexer_5_out2, demultiplexer_5_out3, demultiplexer_5_out4,
       demultiplexer_5_out5, demultiplexer_5_out6, demultiplexer_5_out7, demultiplexer_5_out8,
       demultiplexer_5_out9, demultiplexer_5_out10, demultiplexer_5_out11, demultiplexer_5_out12,
       demultiplexer_5_out13, demultiplexer_5_out14, demultiplexer_5_out15, demultiplexer_5_out16,
       demultiplexer_5_out17, demultiplexer_5_out18, demultiplexer_5_out19, demultiplexer_5_out20,
       demultiplexer_5_out21, demultiplexer_5_out22, demultiplexer_5_out23, demultiplexer_5_out24,
       demultiplexer_5_out25, demultiplexer_5_out26, demultiplexer_5_out27, demultiplexer_5_out28,
       demultiplexer_5_out29, demultiplexer_5_out30, demultiplexer_5_out31, multiplexer_2_out,
       multiplexer_3_out, multiplexer_4_out, register_1_q, register_3_q, xor_1_out;
  wire [7:1] and_6_out, controlled_inverter_1_out;
  wire [9:0] and_1_out, and_2_out, and_3_out, and_4_out, and_5_out, multiplexer_1_out, P_out;

  DotMatrix #(.matrixcols(32), .matrixrows(8), .persist(540)) dotmatrix_1 (
    .col0(demultiplexer_1_out0), .col1(demultiplexer_1_out1), .col2(demultiplexer_1_out2),
    .col3(demultiplexer_1_out3), .col4(demultiplexer_1_out4), .col5(demultiplexer_1_out5),
    .col6(demultiplexer_1_out6), .col7(demultiplexer_1_out7), .col8(demultiplexer_1_out8),
    .col9(demultiplexer_1_out9), .col10(demultiplexer_1_out10), .col11(demultiplexer_1_out11),
    .col12(demultiplexer_1_out12), .col13(demultiplexer_1_out13), .col14(demultiplexer_1_out14),
    .col15(demultiplexer_1_out15), .col16(demultiplexer_1_out16), .col17(demultiplexer_1_out17),
    .col18(demultiplexer_1_out18), .col19(demultiplexer_1_out19), .col20(demultiplexer_1_out20),
    .col21(demultiplexer_1_out21), .col22(demultiplexer_1_out22), .col23(demultiplexer_1_out23),
    .col24(demultiplexer_1_out24), .col25(demultiplexer_1_out25), .col26(demultiplexer_1_out26),
    .col27(demultiplexer_1_out27), .col28(demultiplexer_1_out28), .col29(demultiplexer_1_out29),
    .col30(demultiplexer_1_out30), .col31(demultiplexer_1_out31));
  Multiplexer #(.enable("false"), .width(10)) multiplexer_1 (
    .in0({P_out[9:6], U_out, N_out, P_out[0]}), .in1(10'h260), .out(multiplexer_1_out), .sel(rst_out));
  Button u_rst (.out(rst_out));
  LED led_1 (.in(Keypad[4]));
  LED led_2 (.in(Keypad[3]));
  Button Ctl (.out(P_out[6]));
  Button U (.out(U_out[0]));
  Button W (.out(P_out[7]));
  Button T (.out(U_out[1]));
  Button S (.out(P_out[8]));
  Button u_D (.out(U_out[2]));
  Button Alt (.out(P_out[9]));
  assign and_1_out = multiplexer_1_out & 10'h225;  // AND_Gate and_1, 10 bits wide
  assign and_2_out = multiplexer_1_out & 10'h312;  // AND_Gate and_2, 10 bits wide
  assign and_3_out = multiplexer_1_out & 10'h1a8;  // AND_Gate and_3, 10 bits wide
  assign and_4_out = multiplexer_1_out & 10'hd4;  // AND_Gate and_4, 10 bits wide
  assign and_5_out = multiplexer_1_out & 10'h4b;  // AND_Gate and_5, 10 bits wide
  Demultiplexer #(.enable("false"), .select(5), .width(8)) demultiplexer_1 (
    .out0(demultiplexer_1_out0), .out1(demultiplexer_1_out1), .out2(demultiplexer_1_out2),
    .out3(demultiplexer_1_out3), .out4(demultiplexer_1_out4), .out5(demultiplexer_1_out5),
    .out6(demultiplexer_1_out6), .out7(demultiplexer_1_out7), .out8(demultiplexer_1_out8),
    .out9(demultiplexer_1_out9), .out10(demultiplexer_1_out10), .out11(demultiplexer_1_out11),
    .out12(demultiplexer_1_out12), .out13(demultiplexer_1_out13), .out14(demultiplexer_1_out14),
    .out15(demultiplexer_1_out15), .out16(demultiplexer_1_out16), .out17(demultiplexer_1_out17),
    .out18(demultiplexer_1_out18), .out19(demultiplexer_1_out19), .out20(demultiplexer_1_out20),
    .out21(demultiplexer_1_out21), .out22(demultiplexer_1_out22), .out23(demultiplexer_1_out23),
    .out24(demultiplexer_1_out24), .out25(demultiplexer_1_out25), .out26(demultiplexer_1_out26),
    .out27(demultiplexer_1_out27), .out28(demultiplexer_1_out28), .out29(demultiplexer_1_out29),
    .out30(demultiplexer_1_out30), .out31(demultiplexer_1_out31), .in(demultiplexer_3_out0), .sel(MUX1));
  LED led_3 (.in(Keypad[2]));
  Button N (.out(N_out[0]));
  Button E (.out(N_out[1]));
  Comparator #(.width(10)) comparator_1 (.a(and_1_out), .b({10{1'b0}}), .eq(Keypad[0]));  // open: gt, lt
  Comparator #(.width(10)) comparator_2 (.a(and_2_out), .b({10{1'b0}}), .eq(Keypad[1]));  // open: gt, lt
  Comparator #(.width(10)) comparator_3 (.a(and_3_out), .b({10{1'b0}}), .eq(Keypad[2]));  // open: gt, lt
  Comparator #(.width(10)) comparator_4 (.a(and_4_out), .b({10{1'b0}}), .eq(Keypad[3]));  // open: gt, lt
  Comparator #(.width(10)) comparator_5 (.a(and_5_out), .b({10{1'b0}}), .eq(Keypad[4]));  // open: gt, lt
  LED led_4 (.in(Keypad[1]));
  LED led_5 (.in(Keypad[0]));
  Button P (.out(P_out[0]));
  DotMatrix #(.matrixcols(32), .matrixrows(8), .persist(540)) dotmatrix_2 (
    .col0(demultiplexer_2_out0), .col1(demultiplexer_2_out1), .col2(demultiplexer_2_out2),
    .col3(demultiplexer_2_out3), .col4(demultiplexer_2_out4), .col5(demultiplexer_2_out5),
    .col6(demultiplexer_2_out6), .col7(demultiplexer_2_out7), .col8(demultiplexer_2_out8),
    .col9(demultiplexer_2_out9), .col10(demultiplexer_2_out10), .col11(demultiplexer_2_out11),
    .col12(demultiplexer_2_out12), .col13(demultiplexer_2_out13), .col14(demultiplexer_2_out14),
    .col15(demultiplexer_2_out15), .col16(demultiplexer_2_out16), .col17(demultiplexer_2_out17),
    .col18(demultiplexer_2_out18), .col19(demultiplexer_2_out19), .col20(demultiplexer_2_out20),
    .col21(demultiplexer_2_out21), .col22(demultiplexer_2_out22), .col23(demultiplexer_2_out23),
    .col24(demultiplexer_2_out24), .col25(demultiplexer_2_out25), .col26(demultiplexer_2_out26),
    .col27(demultiplexer_2_out27), .col28(demultiplexer_2_out28), .col29(demultiplexer_2_out29),
    .col30(demultiplexer_2_out30), .col31(demultiplexer_2_out31));
  Clock #(.highDuration(2), .lowDuration(2)) clock_1 (.out(clk1));
  Clock #(.highDuration(2), .lowDuration(2), .phaseOffset(3)) clock_2 (.out(clk2));
  Clock clock_3 (.out(clk0));
  Button button_1 (.out(button_1_out));
  Counter #(.max('h87)) counter_1 (.Q(counter_1_q), .clk(clk1), .clr(rst));  // open: load, D, count, carry, up
  D_Flip_Flop d_ff_1 (.clk(clk0), .D(1'b1), .Q(run), .Qn(rst), .reset(button_1_out));  // open: preset
  Register register_1 (.D(D), .Q(register_1_q), .clk(clock_4_out));  // open: en, clr
  Clock clock_4 (.out(clock_4_out));
  Register #(.trigger("falling")) register_2 (.D(counter_1_q), .Q({MUX2, MUX1}), .clk(clk1));  // open: en, clr
  Comparator #(.width(7)) comparator_6 (.a(counter_1_q[7:1]), .b(7'b1000000), .eq(comparator_6_eq));  // open: gt, lt
  Counter #(.max('h87)) counter_2 (.Q(counter_2_q), .clk(clk1), .clr(rst));  // open: load, D, count, carry, up
  Demultiplexer #(.enable("false"), .select(5), .width(8)) demultiplexer_2 (
    .out0(demultiplexer_2_out0), .out1(demultiplexer_2_out1), .out2(demultiplexer_2_out2),
    .out3(demultiplexer_2_out3), .out4(demultiplexer_2_out4), .out5(demultiplexer_2_out5),
    .out6(demultiplexer_2_out6), .out7(demultiplexer_2_out7), .out8(demultiplexer_2_out8),
    .out9(demultiplexer_2_out9), .out10(demultiplexer_2_out10), .out11(demultiplexer_2_out11),
    .out12(demultiplexer_2_out12), .out13(demultiplexer_2_out13), .out14(demultiplexer_2_out14),
    .out15(demultiplexer_2_out15), .out16(demultiplexer_2_out16), .out17(demultiplexer_2_out17),
    .out18(demultiplexer_2_out18), .out19(demultiplexer_2_out19), .out20(demultiplexer_2_out20),
    .out21(demultiplexer_2_out21), .out22(demultiplexer_2_out22), .out23(demultiplexer_2_out23),
    .out24(demultiplexer_2_out24), .out25(demultiplexer_2_out25), .out26(demultiplexer_2_out26),
    .out27(demultiplexer_2_out27), .out28(demultiplexer_2_out28), .out29(demultiplexer_2_out29),
    .out30(demultiplexer_2_out30), .out31(demultiplexer_2_out31), .in(demultiplexer_3_out1), .sel(MUX1));
  // NOT_Gate not_1 has open pins: in=1'b0, out=open
  Multiplexer #(.enable("false"), .width(8)) multiplexer_2 (
    .in0(8'h6a), .in1(multiplexer_3_out), .out(multiplexer_2_out));  // open: sel
  Multiplexer #(.enable("false"), .width(8)) multiplexer_3 (
    .in0(D), .in1(register_1_q), .out(multiplexer_3_out));  // open: sel
  assign not_2_out = ~Keypad;  // NOT_Gate not_2, 5 bits wide
  nor nor_1 (nor_1_out, counter_1_q[1], comparator_6_eq);
  Shift_Register #(.trigger("falling")) shift_register_1 (
    .shift(1'b1), .in(nor_1_out), .clk(clk1), .q1(shift_register_1_q1[0]), .q4(shift_register_1_q1[1]));  // open: out, load, clr, d0, q0, d1, d2, q2, d3, q3, d4, d5, q5, d6, q6, d7, q7
  Adder adder_1 (.a(counter_2_q), .b({8{1'b0}}), .out(adder_1_out));  // open: cin, cout
  assign {and_6_out, Q0} = adder_1_out & 8'h7f;  // AND_Gate and_6, 8 bits wide
  DotMatrix #(.matrixcols(32), .matrixrows(8), .persist(540)) dotmatrix_3 (
    .col0(demultiplexer_4_out0), .col1(demultiplexer_4_out1), .col2(demultiplexer_4_out2),
    .col3(demultiplexer_4_out3), .col4(demultiplexer_4_out4), .col5(demultiplexer_4_out5),
    .col6(demultiplexer_4_out6), .col7(demultiplexer_4_out7), .col8(demultiplexer_4_out8),
    .col9(demultiplexer_4_out9), .col10(demultiplexer_4_out10), .col11(demultiplexer_4_out11),
    .col12(demultiplexer_4_out12), .col13(demultiplexer_4_out13), .col14(demultiplexer_4_out14),
    .col15(demultiplexer_4_out15), .col16(demultiplexer_4_out16), .col17(demultiplexer_4_out17),
    .col18(demultiplexer_4_out18), .col19(demultiplexer_4_out19), .col20(demultiplexer_4_out20),
    .col21(demultiplexer_4_out21), .col22(demultiplexer_4_out22), .col23(demultiplexer_4_out23),
    .col24(demultiplexer_4_out24), .col25(demultiplexer_4_out25), .col26(demultiplexer_4_out26),
    .col27(demultiplexer_4_out27), .col28(demultiplexer_4_out28), .col29(demultiplexer_4_out29),
    .col30(demultiplexer_4_out30), .col31(demultiplexer_4_out31));
  Demultiplexer #(.enable("false"), .select(3), .width(8)) demultiplexer_3 (
    .out0(demultiplexer_3_out0), .out1(demultiplexer_3_out1), .out2(demultiplexer_3_out2),
    .out3(demultiplexer_3_out3), .in({controlled_inverter_1_out, 1'b0}), .sel(MUX2));  // open: out4, out5, out6, out7
  // Probe on {De[6:0], D}
  ROM #(.addrWidth(15)) AdventText (.addr({De[6:0], D}), .data(AdventText_data));
  // Probe on {not_2_out[4:3], 1'b1, not_2_out[0], 1'b1, not_2_out[1], not_2_out[2], multiplexer_2_out}
  ROM #(.addrWidth(15)) LedCube (
    .addr({not_2_out[4:3], 1'b1, not_2_out[0], 1'b1, not_2_out[1], not_2_out[2], multiplexer_2_out}), .data(D));
  Multiplexer #(.enable("false"), .width(8)) multiplexer_4 (
    .in0({8{1'b1}}), .in1(De), .out(multiplexer_4_out), .sel(run));
  ROM #(.addrWidth(15)) encoder (.addr({{5{1'b1}}, shift_register_1_q1, multiplexer_4_out}), .data(De));
  assign xor_1_out = {1'b0, and_6_out} ^ ~{and_6_out, Q0};  // XOR_Gate xor_1, 8 bits wide
  // Probe on register_3_q
  Register #(.trigger("falling")) register_3 (.D(xor_1_out), .Q(register_3_q), .clk(clk1));  // open: en, clr
  Demultiplexer #(.enable("false"), .select(5), .width(8)) demultiplexer_4 (
    .out0(demultiplexer_4_out0), .out1(demultiplexer_4_out1), .out2(demultiplexer_4_out2),
    .out3(demultiplexer_4_out3), .out4(demultiplexer_4_out4), .out5(demultiplexer_4_out5),
    .out6(demultiplexer_4_out6), .out7(demultiplexer_4_out7), .out8(demultiplexer_4_out8),
    .out9(demultiplexer_4_out9), .out10(demultiplexer_4_out10), .out11(demultiplexer_4_out11),
    .out12(demultiplexer_4_out12), .out13(demultiplexer_4_out13), .out14(demultiplexer_4_out14),
    .out15(demultiplexer_4_out15), .out16(demultiplexer_4_out16), .out17(demultiplexer_4_out17),
    .out18(demultiplexer_4_out18), .out19(demultiplexer_4_out19), .out20(demultiplexer_4_out20),
    .out21(demultiplexer_4_out21), .out22(demultiplexer_4_out22), .out23(demultiplexer_4_out23),
    .out24(demultiplexer_4_out24), .out25(demultiplexer_4_out25), .out26(demultiplexer_4_out26),
    .out27(demultiplexer_4_out27), .out28(demultiplexer_4_out28), .out29(demultiplexer_4_out29),
    .out30(demultiplexer_4_out30), .out31(demultiplexer_4_out31), .in(demultiplexer_3_out2), .sel(MUX1));
  assign {controlled_inverter_1_out[1], controlled_inverter_1_out[2], controlled_inverter_1_out[3], controlled_inverter_1_out[4], controlled_inverter_1_out[5], controlled_inverter_1_out[6], controlled_inverter_1_out[7]} = not_3_out ? ~AdventText_data[6:0] : 7'bz;  // Controlled_Inverter controlled_inverter_1
  not not_3 (not_3_out, clk2);
  LED led_6 (.in(AdventText_data[7]));
  // Probe on D
  // Probe on De
  DotMatrix #(.matrixcols(32), .matrixrows(8), .persist(540)) dotmatrix_4 (
    .col0(demultiplexer_5_out0), .col1(demultiplexer_5_out1), .col2(demultiplexer_5_out2),
    .col3(demultiplexer_5_out3), .col4(demultiplexer_5_out4), .col5(demultiplexer_5_out5),
    .col6(demultiplexer_5_out6), .col7(demultiplexer_5_out7), .col8(demultiplexer_5_out8),
    .col9(demultiplexer_5_out9), .col10(demultiplexer_5_out10), .col11(demultiplexer_5_out11),
    .col12(demultiplexer_5_out12), .col13(demultiplexer_5_out13), .col14(demultiplexer_5_out14),
    .col15(demultiplexer_5_out15), .col16(demultiplexer_5_out16), .col17(demultiplexer_5_out17),
    .col18(demultiplexer_5_out18), .col19(demultiplexer_5_out19), .col20(demultiplexer_5_out20),
    .col21(demultiplexer_5_out21), .col22(demultiplexer_5_out22), .col23(demultiplexer_5_out23),
    .col24(demultiplexer_5_out24), .col25(demultiplexer_5_out25), .col26(demultiplexer_5_out26),
    .col27(demultiplexer_5_out27), .col28(demultiplexer_5_out28), .col29(demultiplexer_5_out29),
    .col30(demultiplexer_5_out30), .col31(demultiplexer_5_out31));
  xor odd_parity_1 (odd_parity_1_out, De[0], De[1], De[2], De[3], De[5], De[6], De[7]);
  Demultiplexer #(.enable("false"), .select(5), .width(8)) demultiplexer_5 (
    .out0(demultiplexer_5_out0), .out1(demultiplexer_5_out1), .out2(demultiplexer_5_out2),
    .out3(demultiplexer_5_out3), .out4(demultiplexer_5_out4), .out5(demultiplexer_5_out5),
    .out6(demultiplexer_5_out6), .out7(demultiplexer_5_out7), .out8(demultiplexer_5_out8),
    .out9(demultiplexer_5_out9), .out10(demultiplexer_5_out10), .out11(demultiplexer_5_out11),
    .out12(demultiplexer_5_out12), .out13(demultiplexer_5_out13), .out14(demultiplexer_5_out14),
    .out15(demultiplexer_5_out15), .out16(demultiplexer_5_out16), .out17(demultiplexer_5_out17),
    .out18(demultiplexer_5_out18), .out19(demultiplexer_5_out19), .out20(demultiplexer_5_out20),
    .out21(demultiplexer_5_out21), .out22(demultiplexer_5_out22), .out23(demultiplexer_5_out23),
    .out24(demultiplexer_5_out24), .out25(demultiplexer_5_out25), .out26(demultiplexer_5_out26),
    .out27(demultiplexer_5_out27), .out28(demultiplexer_5_out28), .out29(demultiplexer_5_out29),
    .out30(demultiplexer_5_out30), .out31(demultiplexer_5_out31), .in(demultiplexer_3_out3), .sel(MUX1));
  // Digital_Oscilloscope digital_oscilloscope_1: pin names not known; wires that end beside it: clk0, clk1, clk2, Q0, odd_parity_1_out

  // Notes on the sheet:
  //   contents of AdventText (hex, n*v repeats v):
  //   ff 7f 7f ff 7f ff ff 7f 7f ff ff 7f ff 7f 7f ff 7f ff ff 7f ff 7f 7f ff ff 7f 7f ff 7f ff ff 7f 7f
  //   80 80 0 f8 0 78 80 80 0 7f c1 7f 80 fe 41 b7 47 47 b7 47 b7 c7 7f 7f c7 c7 7f c7 7f 7f c7 7f ff ff
  //   7f ff 7f 7f ff ff 7f 7f ff 7f ff ff 7f ff 7f 7f ff 7f ff ff 7f 7f ff ff 7f ff 7f 7f ff ff 0 0 80 78
  //   80 f8 0 0 80 eb 41 ff 0 7e c1 41 ff ff 41 ff 0 41 80 c1 41 7f fe 0 80 ff 7f 7f ff ff 7f ff 7f 7f ff
  //   ff 7f 7f ff 7f ff ff 7f ff 7f 7f ff 7f ff ff 7f 7f ff ff 7f ff 7f 7f ff ff 0 0 80 78 80 f8 0 0 80 ff
  //   41 ff 0 7e c1 47 b7 b7 47 b7 47 7f c7 c7 7f 7f c7 7f c7 c7 7f ff 7f 7f ff 7f ff ff 7f 7f ff ff 7f ff
  //   7f 7f ff 7f ff ff 7f ff 7f 7f ff ff 7f 7f ff 7f ff ff 7f 7f 80 80 0 f8 0 78 80 80 0 6b c1 7f 80 fe
  //   41 ff 41 41 ff 7f 80 c1 7f 41 ff ff 41 80 0 7f ff ff 7f 7f ff 7f ff ff 7f 7f ff ff 7f ff 7f 7f ff 7f
  //   ff ff 7f ff 7f 7f ff ff 7f 7f ff 7f ff ff 7f 7f ff ff 7f ff 7f 7f ff ff 7f 7f ff 7f ff ff 7f ff 7f
  //   7f ff 7f ff ff 7f 7f ff ff 7f ff 7f 7f ff 7f ff ff 7f ff 7f 7f ff ff 7f 7f ff 7f ff ff 7f ff 7f 7f
  //   ff 7f ff ff 7f 7f ff ff 7f ff 7f 7f ff ff 7f 7f ff 7f ff ff 7f 7f ff ff 7f ff 7f 7f ff 7f ff ff 7f
  //   ff 7f 7f ff ff 7f 7f ff 7f ff ff 7f 7f ff ff 7f ff 7f 7f ff ff 7f 7f ff 7f ff ff 7f ff 7f 7f ff 7f
  //   ff ff 7f 7f ff ff 7f ff 7f 7f ff ff 7f 7f ff 7f ff ff 7f 7f ff ff 7f ff 7f 7f ff 7f ff ff 7f ff 7f
  //   7f ff ff 7f 7f ff 7f ff ff 7f ff 7f 7f ff 7f ff ff 7f 7f ff ff 7f ff 7f 7f ff 7f ff ff 7f ff 7f 7f
  //   ff ff 7f 7f ff 7f ff ff 7f 7f ff ff 7f ff 7f 7f ff ff 7f 7f ff 7f ff ff 7f ff 7f 7f ff 7f ff ff 7f
  //   7f ff ff 7f ff 7f 7f ff ff 7f 7f ff 7f ff ff 7f 7f ff ff 7f ff 7f 7f ff 7f ff ff 7f ff 7f 7f ff ff
  //   7f 7f ff 7f ff ff 7f 7f bf b6 3f f7 3f 77 b6 fb 3f 7f be 7f b6 fe 3e ab 3b 3b ab 3b ab ab 3e 3e ab
  //   ab 3e ab 3e 3e ab 7f ff ff 7f ff 7f 7f ff ff 7f 7f ff 7f ff ff 7f ff 7f 7f ff 7f ff ff 7f 7f ff ff
  //   7f ff 7f 7f ff ff 3f 36 bf 77 bf f7 36 7b bf eb 3e ff 36 7e be 3e 9f 9f 3e ff 3f 3e bf be 3e 7f fe
  //   3f bf ff 7f 7f ff ff 7f ff 7f 7f ff ff 7f 7f ff 7f ff ff 7f ff 7f 7f ff 7f ff ff 7f 7f ff ff 7f ff
  //   7f 7f ff ff 3f 36 bf 77 bf f7 36 7b bf ff 3e ff 36 7e be 3b ab ab 3b ab 3b 3e ab ab 3e 3e ab 3e ab
  //   ab 3e ff 7f 7f ff 7f ff ff 7f 7f ff ff 7f ff 7f 7f ff 7f ff ff 7f ff 7f 7f ff ff 7f 7f ff 7f ff ff
  //   7f 7f bf b6 3f f7 3f 77 b6 fb 3f 6b be 7f b6 fe 3e f8 3e 3e 9f 7f bf be 7f 3e 9f be 3e bf 3f 7f ff
  //   ff 7f 7f ff 7f ff ff 7f 7f ff ff 7f ff 7f 7f ff 7f ff ff 7f ff 7f 7f ff ff 7f 7f ff 7f ff ff 7f 7f
  //   bf b6 3f 8f 3f f b6 f7 3f 7f b6 7f b6 80 36 ab 3b 3b ab 3b ab ab 5d 5d ab ab 5d ab 5d 5d ab 7f ff ff
  //   7f ff 7f 7f ff ff 7f 7f ff 7f ff ff 7f ff 7f 7f ff 7f ff ff 7f 7f ff ff 7f ff 7f 7f ff ff 3f 36 bf f
  //   bf 8f 36 77 bf eb 36 ff 36 0 b6 3e 9f 9f 3e ff 3f 3e bf be 3e 7f 80 3f bf ff 7f 7f ff ff 7f ff 7f 7f
  //   ff ff 7f 7f ff 7f ff ff 7f ff 7f 7f ff 7f ff ff 7f 7f ff ff 7f ff 7f 7f ff ff 3f 36 bf f bf 8f 36 77
  //   bf ff 36 ff 36 0 b6 3b ab ab 3b ab 3b 5d ab ab 5d 5d ab 5d ab ab 5d ff 7f 7f ff 7f ff ff 7f 7f ff ff
  //   7f ff 7f 7f ff 7f ff ff 7f ff 7f 7f ff ff 7f 7f ff 7f ff ff 7f 7f bf b6 3f 8f 3f f b6 f7 3f 6b b6 7f
  //   b6 80 36 ff 3e 3e 9f 7f bf be 7f 3e 9f 80 3e bf 3f 7f ff ff 7f 7f ff 7f ff ff 7f 7f ff ff 7f ff 7f
  //   7f ff 7f ff ff 7f ff 7f 7f ff ff 7f 7f ff 7f ff ff 7f 7f fe ba 7e fe 7e 7e ba be 7e 7f ef 7f ba f6
  //   6f ab 2b 2b ab 2b ab ab 37 37 ab ab 37 ab 37 37 ab 7f ff ff 7f ff 7f 7f ff ff 7f 7f ff 7f ff ff 7f
  //   ff 7f 7f ff 7f ff ff 7f 7f ff ff 7f ff 7f 7f ff ff 7e 3a fe 7e fe fe 3a 3e fe ef 6f ff 3a 3f ef 56
  //   ef ef 56 fe 7f 6f bf be 56 6f ff 7f ff ff 7f 7f ff ff 7f ff 7f 7f ff ff 7f 7f ff 7f ff ff 7f ff 7f
  //   7f ff 7f ff ff 7f 7f ff ff 7f ff 7f 7f ff ff 7e 3a fe 7e fe fe 3a 3e fe ff 6f ff 3a 76 ef 2b ab ab
  //   2b ab 2b 37 ab ab 37 37 ab 37 ab ab 37 ff 7f 7f ff 7f ff ff 7f 7f ff ff 7f ff 7f 7f ff 7f ff ff 7f
  //   ff 7f 7f ff ff 7f 7f ff 7f ff ff 7f 7f fe ba 7e fe 7e 7e ba be 7e 6f ef 7f ba bf 6f eb 56 56 ef 7e
  //   ff ef 7f 3e ef be 56 ff 7f 7f ff ff 7f 7f ff 7f ff ff 7f 7f ff ff 7f ff 7f 7f ff 7f ff ff 7f ff 7f
  //   7f ff ff 7f 7f ff 7f ff ff 7f 7f fe bc 7e fe 7e 7e bc c1 7e 7f 80 7f bc 81 0 87 67 67 87 67 87 df 0
  //   0 df df 0 df 0 0 df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
  //   contents of LedCube (hex, n*v repeats v):
  //   0 81 82 3 84 5 6 87 88 9 a 8b c 8d 8e f 90 11 12 93 14 95 96 17 18 99 9a 1b 9c 1d 1e 9f a0 21 22 a3
  //   24 a5 a6 27 28 a9 aa 2b ac 2d 2e af 30 b1 b2 33 b4 35 36 b7 b8 39 3a bb 3c bd be 3f c0 41 42 c3 44
  //   c5 c6 47 48 c9 ca 4b cc 4d 4e cf 50 d1 d2 53 d4 55 56 d7 d8 59 5a db 5c dd de 5f 60 e1 e2 63 e4 65
  //   66 e7 e8 69 6a eb 6c ed ee 6f f0 71 72 f3 74 f5 f6 77 78 f9 fa 7b fc 7d 7e ff 0 81 82 3 84 5 6 87 88
  //   9 a 8b c 8d 8e f 90 11 12 93 14 95 96 17 18 99 9a 1b 9c 1d 1e 9f a0 21 22 a3 24 a5 a6 27 28 a9 aa 2b
  //   ac 2d 2e af 30 b1 b2 33 b4 35 36 b7 b8 39 3a bb 3c bd be 3f c0 41 42 c3 44 c5 c6 47 48 c9 ca 4b cc
  //   4d 4e cf 50 d1 d2 53 d4 55 56 d7 d8 59 5a db 5c dd de 5f 60 e1 e2 63 e4 65 66 e7 e8 69 6a eb 6c ed
  //   ee 6f f0 71 72 f3 74 f5 f6 77 78 f9 fa 7b fc 7d 7e ff 0 1 2 3 4 5 6 7 8 9 a b c d e f 10 11 12 13 14
  //   15 16 17 18 19 1a 1b 1c 1d 1e 1f 20 21 22 23 24 25 26 27 28 29 2a 2b 2c 2d 2e 2f 30 31 32 33 34 35
  //   36 37 38 39 3a 3b 3c 3d 3e 3f 40 41 42 43 44 45 46 47 48 49 4a 4b 4c 4d 4e 4f 50 51 52 53 54 55 56
  //   57 58 59 5a 5b 5c 5d 5e 5f 60 61 62 63 64 65 66 67 68 69 6a 6b 6c 6d 6e 6f 70 71 72 73 74 75 76 77
  //   78 79 7a 7b 7c 7d 7e 7f 80 81 82 83 84 85 86 87 88 89 8a 8b 8c 8d 8e 8f 90 91 92 93 94 95 96 97 98
  //   99 9a 9b 9c 9d 9e 9f a0 a1 a2 a3 a4 a5 a6 a7 a8 a9 aa ab ac ad ae af b0 b1 b2 b3 b4 b5 b6 b7 b8 b9
  //   ba bb bc bd be bf c0 c1 c2 c3 c4 c5 c6 c7 c8 c9 ca cb cc cd ce cf d0 d1 d2 d3 d4 d5 d6 d7 d8 d9 da
  //   db dc dd de df e0 e1 e2 e3 e4 e5 e6 e7 e8 e9 ea eb ec ed ee ef f0 f1 f2 f3 f4 f5 f6 f7 f8 f9 fa fb
  //   fc fd fe ff 0 1 2 3 4 5 6 7 8 9 a b c d e f 10 11 12 13 14 15 16 17 18 19 1a 1b 1c 1d 1e 1f 20 21 22
  //   23 24 25 26 27 28 29 2a 2b 2c 2d 2e 2f 30 31 32 33 34 35 36 37 38 39 3a 3b 3c 3d 3e 3f 40 41 42 43
  //   44 45 46 47 48 49 4a 4b 4c 4d 4e 4f 50 51 52 53 54 55 56 57 58 59 5a 5b 5c 5d 5e 5f 60 61 62 63 64
  //   65 66 67 68 69 6a 6b 6c 6d 6e 6f 70 71 72 73 74 75 76 77 78 79 7a 7b 7c 7d 7e 7f 80 81 82 83 84 85
  //   86 87 88 89 8a 8b 8c 8d 8e 8f 90 91 92 93 94 95 96 97 98 99 9a 9b 9c 9d 9e 9f a0 a1 a2 a3 a4 a5 a6
  //   a7 a8 a9 aa ab ac ad ae af b0 b1 b2 b3 b4 b5 b6 b7 b8 b9 ba bb bc bd be bf c0 c1 c2 c3 c4 c5 c6 c7
  //   c8 c9 ca cb cc cd ce cf d0 d1 d2 d3 d4 d5 d6 d7 d8 d9 da db dc dd de df e0 e1 e2 e3 e4 e5 e6 e7 e8
  //   e9 ea eb ec ed ee ef f0 f1 f2 f3 f4 f5 f6 f7 f8 f9 fa fb fc fd fe ff 10 1 2 1 4 15 4 7 8 19 8 b 1c d
  //   e d 10 13 2 13 16 15 16 7 1a 19 1a b 1c 1f e 1f 20 31 20 23 34 25 26 25 38 29 2a 29 2c 3d 2c 2f 32
  //   31 32 23 34 37 26 37 38 3b 2a 3b 3e 3d 3e 2f 40 51 40 43 54 45 46 45 58 49 4a 49 4c 5d 4c 4f 52 51
  //   52 43 54 57 46 57 58 5b 4a 5b 5e 5d 5e 4f 70 61 62 61 64 75 64 67 68 79 68 6b 7c 6d 6e 6d 70 73 62
  //   73 76 75 76 67 7a 79 7a 6b 7c 7f 6e 7f 80 91 80 83 94 85 86 85 98 89 8a 89 8c 9d 8c 8f 92 91 92 83
  //   94 97 86 97 98 9b 8a 9b 9e 9d 9e 8f b0 a1 a2 a1 a4 b5 a4 a7 a8 b9 a8 ab bc ad ae ad b0 b3 a2 b3 b6
  //   b5 b6 a7 ba b9 ba ab bc bf ae bf d0 c1 c2 c1 c4 d5 c4 c7 c8 d9 c8 cb dc cd ce cd d0 d3 c2 d3 d6 d5
  //   d6 c7 da d9 da cb dc df ce df e0 f1 e0 e3 f4 e5 e6 e5 f8 e9 ea e9 ec fd ec ef f2 f1 f2 e3 f4 f7 e6
  //   f7 f8 fb ea fb fe fd fe ef 1024*ff 0 1 2 3 4 5 6 7 8 9 a b c d e f 10 11 12 13 14 15 16 17 18 19 1a
  //   1b 1c 1d 1e 1f 20 21 22 23 24 25 26 27 28 29 2a 2b 2c 2d 2e 2f 30 31 32 33 34 35 36 37 38 39 3a 3b
  //   3c 3d 3e 3f 40 41 42 43 44 45 46 47 48 49 4a 4b 4c 4d 4e 4f 50 51 52 53 54 55 56 57 58 59 5a 5b 5c
  //   5d 5e 5f 60 61 62 63 64 65 66 67 68 69 6a 6b 6c 6d 6e 6f 70 71 72 73 74 75 76 77 78 79 7a 7b 7c 7d
  //   7e 7f 80 81 82 83 84 85 86 87 88 89 8a 8b 8c 8d 8e 8f 90 91 92 93 94 95 96 97 98 99 9a 9b 9c 9d 9e
  //   9f a0 a1 a2 a3 a4 a5 a6 a7 a8 a9 aa ab ac ad ae af b0 b1 b2 b3 b4 b5 b6 b7 b8 b9 ba bb bc bd be bf
  //   c0 c1 c2 c3 c4 c5 c6 c7 c8 c9 ca cb cc cd ce cf d0 d1 d2 d3 d4 d5 d6 d7 d8 d9 da db dc dd de df e0
  //   e1 e2 e3 e4 e5 e6 e7 e8 e9 ea eb ec ed ee ef f0 f1 f2 f3 f4 f5 f6 f7 f8 f9 fa fb fc fd fe ff 20 1 2
  //   23 4 1 2 7 8 29 2a b 8 d e b 10 31 32 13 10 15 16 13 38 19 1a 3b 1c 19 1a 1f 20 25 26 23 4 25 26 7
  //   2c 29 2a 2f 2c d e 2f 34 31 32 37 34 15 16 37 38 3d 3e 3b 1c 3d 3e 1f 40 61 62 43 40 45 46 43 68 49
  //   4a 6b 4c 49 4a 4f 70 51 52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
  //   contents of encoder (hex, n*v repeats v):
  //   29696*ff 0 1 0 b 6 1 6 7 a d a b c d c 2f 12 15 12 13 14 15 14 7 18 19 18 13 1e 19 1e 1f 22 25 22 23
  //   24 25 24 37 28 29 28 23 2e 29 2e 2f 30 31 30 3b 36 31 36 37 3a 3d 3a 3b 3c 3d 3c bf 42 45 42 43 44
  //   45 44 57 48 49 48 43 4e 49 4e 4f 50 51 50 5b 56 51 56 57 5a 5d 5a 5b 5c 5d 5c 1f 60 61 60 6b 66 61
  //   66 67 6a 6d 6a 6b 6c 6d 6c 4f 72 75 72 73 74 75 74 67 78 79 78 73 7e 79 7e 7f 82 85 82 83 84 85 84
  //   97 88 89 88 83 8e 89 8e 8f 90 91 90 9b 96 91 96 97 9a 9d 9a 9b 9c 9d 9c df a0 a1 a0 ab a6 a1 a6 a7
  //   aa ad aa ab ac ad ac 8f b2 b5 b2 b3 b4 b5 b4 a7 b8 b9 b8 b3 be b9 be bf c0 c1 c0 cb c6 c1 c6 c7 ca
  //   cd ca cb cc cd cc ef d2 d5 d2 d3 d4 d5 d4 c7 d8 d9 d8 d3 de d9 de df e2 e5 e2 e3 e4 e5 e4 f7 e8 e9
  //   e8 e3 ee e9 ee ef f0 f1 f0 fb f6 f1 f6 f7 fa fd fa fb fc fd fc fd 0 0 2 2 4 4 6 6 8 8 a a c c e e 10
  //   10 12 12 14 14 16 16 18 18 1a 1a 1c 1c 1e 1e 20 20 22 22 24 24 26 26 28 28 2a 2a 2c 2c 2e 2e 30 30
  //   32 32 34 34 36 36 38 38 3a 3a 3c 3c 3e 3e 40 40 42 42 44 44 46 46 48 48 4a 4a 4c 4c 4e 4e 50 50 52
  //   52 54 54 56 56 58 58 5a 5a 5c 5c 5e 5e 60 60 62 62 64 64 66 66 68 68 6a 6a 6c 6c 6e 6e 70 70 72 72
  //   74 74 76 76 78 78 7a 7a 7c 7c 7e 7e 80 80 82 82 84 84 86 86 88 88 8a 8a 8c 8c 8e 8e 90 90 92 92 94
  //   94 96 96 98 98 9a 9a 9c 9c 9e 9e a0 a0 a2 a2 a4 a4 a6 a6 a8 a8 aa aa ac ac ae ae b0 b0 b2 b2 b4 b4
  //   b6 b6 b8 b8 ba ba bc bc be be c0 c0 c2 c2 c4 c4 c6 c6 c8 c8 ca ca cc cc ce ce d0 d0 d2 d2 d4 d4 d6
  //   d6 d8 d8 da da dc dc de de e0 e0 e2 e2 e4 e4 e6 e6 e8 e8 ea ea ec ec ee ee f0 f0 f2 f2 f4 f4 f6 f6
  //   f8 f8 fa fa fc fc fe fe 1 1 3 3 5 5 7 7 9 9 b b d d f f 11 11 13 13 15 15 17 17 19 19 1b 1b 1d 1d 1f
  //   1f 21 21 23 23 25 25 27 27 29 29 2b 2b 2d 2d 2f 2f 31 31 33 33 35 35 37 37 39 39 3b 3b 3d 3d 3f 3f
  //   41 41 43 43 45 45 47 47 49 49 4b 4b 4d 4d 4f 4f 51 51 53 53 55 55 57 57 59 59 5b 5b 5d 5d 5f 5f 61
  //   61 63 63 65 65 67 67 69 69 6b 6b 6d 6d 6f 6f 71 71 73 73 75 75 77 77 79 79 7b 7b 7d 7d 7f 7f 81 81
  //   83 83 85 85 87 87 89 89 8b 8b 8d 8d 8f 8f 91 91 93 93 95 95 97 97 99 99 9b 9b 9d 9d 9f 9f a1 a1 a3
  //   a3 a5 a5 a7 a7 a9 a9 ab ab ad ad af af b1 b1 b3 b3 b5 b5 b7 b7 b9 b9 bb bb bd bd bf bf c1 c1 c3 c3
  //   c5 c5 c7 c7 c9 c9 cb cb cd cd cf cf d1 d1 d3 d3 d5 d5 d7 d7 d9 d9 db db dd dd df df e1 e1 e3 e3 e5
  //   e5 e7 e7 e9 e9 eb eb ed ed ef ef f1 f1 f3 f3 f5 f5 f7 f7 f9 f9 fb fb fd fd ff ff 2 5 2 3 4 5 4 17 8
  //   9 8 3 e 9 e f 10 11 10 1b 16 11 16 17 1a 1d 1a 1b 1c 1d 1c 5f 20 21 20 2b 26 21 26 27 2a 2d 2a 2b 2c
  //   2d 2c f 32 35 32 33 34 35 34 27 38 39 38 33 3e 39 3e 3f 40 41 40 4b 46 41 46 47 4a 4d 4a 4b 4c 4d 4c
  //   6f 52 55 52 53 54 55 54 47 58 59 58 53 5e 59 5e 5f 62 65 62 63 64 65 64 77 68 69 68 63 6e 69 6e 6f
  //   70 71 70 7b 76 71 76 77 7a 7d 7a 7b 7c 7d 7c 7d 80 81 80 8b 86 81 86 87 8a 8d 8a 8b 8c 8d 8c af 92
  //   95 92 93 94 95 94 87 98 99 98 93 9e 99 9e 9f a2 a5 a2 a3 a4 a5 a4 b7 a8 a9 a8 a3 ae a9 ae af b0 b1
  //   b0 bb b6 b1 b6 b7 ba bd ba bb bc bd bc 3f c2 c5 c2 c3 c4 c5 c4 d7 c8 c9 c8 c3 ce c9 ce cf d0 d1 d0
  //   db d6 d1 d6 d7 da dd da db dc dd dc 9f e0 e1 e0 eb e6 e1 e6 e7 ea ed ea eb ec ed ec cf f2 f5 f2 f3
  //   f4 f5 f4 e7 f8 f9 f8 f3 fe f9 fe ff 1 1 3 3 5 5 7 7 9 9 b b d d f f 11 11 13 13 15 15 17 17 19 19 1b
  //   1b 1d 1d 1f 1f 21 21 23 23 25 25 27 27 29 29 2b 2b 2d 2d 2f 2f 31 31 33 33 35 35 37 37 39 39 3b 3b
  //   3d 3d 3f 3f 41 41 43 43 45 45 47 47 49 49 4b 4b 4d 4d 4f 4f 51 51 53 53 55 55 57 57 59 59 5b 5b 5d
  //   5d 5f 5f 61 61 63 63 65 65 67 67 69 69 6b 6b 6d 6d 6f 6f 71 71 73 73 75 75 77 77 79 79 7b 7b 7d 7d
  //   7f 7f 81 81 83 83 85 85 87 87 89 89 8b 8b 8d 8d 8f 8f 91 91 93 93 95 95 97 97 99 99 9b 9b 9d 9d 9f
  //   9f a1 a1 a3 a3 a5 a5 a7 a7 a9 a9 ab ab ad ad af af b1 b1 b3 b3 b5 b5 b7 b7 b9 b9 bb bb bd bd bf bf
  //   c1 c1 c3 c3 c5 c5 c7 c7 c9 c9 cb cb cd cd cf cf d1 d1 d3 d3 d5 d5 d7 d7 d9 d9 db db dd dd df df e1
  //   e1 e3 e3 e5 e5 e7 e7 e9 e9 eb eb ed ed ef ef f1 f1 f3 f3 f5 f5 f7 f7 f9 f9 fb fb fd fd ff ff 0 1 0 b
  //   6 1 6 7 a d a b c d c 2f 12 15 12 13 14 15 14 7 18 19 18 13 1e 19 1e 1f 22 25 22 23 24 25 24 37 28
  //   29 28 23 2e 29 2e 2f 30 31 30 3b 36 31 36 37 3a 3d 3a 3b 3c 3d 3c bf 42 45 42 43 44 45 44 57 48 49
  //   48 43 4e 49 4e 4f 50 51 5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
endmodule

module stepupdown (
  input  up,
  input  down,
  input  reset,
  output phaseA,
  output phaseB
);

  wire not_2_out, not_3_out, or_1_out;
  wire [0:0] not_1_out, not_1_out_2;
  wire [1:0] controlled_buffer_1_out;

  assign {not_1_out_2[0], not_1_out[0]} = ~{phaseB, phaseA};  // NOT_Gate not_1, 2 bits wide
  assign controlled_buffer_1_out = up ? {not_1_out[0], phaseB} : 2'bz;  // Controlled_Buffer controlled_buffer_1
  assign controlled_buffer_1_out = down ? {phaseA, not_1_out_2[0]} : 2'bz;  // Controlled_Buffer controlled_buffer_2
  or or_1 (or_1_out, up, down);
  not not_2 (not_2_out, or_1_out);
  not not_3 (not_3_out, not_2_out);
  Register #(.width(2)) register_1 (
    .D(controlled_buffer_1_out), .clk(not_3_out), .Q({phaseB, phaseA}), .clr(reset));  // open: en
  LED led_1 (.in(phaseA));
  LED led_2 (.in(phaseB));
endmodule
