// Logisim project ledcube.circ as structural Verilog: 1 circuit, main circuit main
module main (
  input  in_1
);

  wire clock_1_out, clock_2_out, multiplexer_3_out, rst_out;
  wire [0:0] xor_2_out, xor_3_out, xor_4_out;
  wire [1:0] demultiplexer_1_out0, demultiplexer_2_out0, demultiplexer_2_out1, demultiplexer_2_out2,
       demultiplexer_2_out3, N_out, rgbled_1_p1, rgbled_2_p1, rgbled_3_p1, rgbled_4_p1, rgbled_5_p1,
       rgbled_6_p1, rgbled_7_p1, rgbled_8_p1, rgbled_9_p1, rgbled_10_p1, rgbled_11_p1, rgbled_12_p1,
       rgbled_13_p1, rgbled_14_p1, rgbled_15_p1, rgbled_16_p1, rgbled_17_p1, rgbled_18_p1, rgbled_19_p1,
       rgbled_20_p1, rgbled_21_p1, rgbled_22_p1, rgbled_23_p1, rgbled_24_p1, rgbled_25_p1, rgbled_26_p1,
       rgbled_27_p1, rgbled_28_p1, rgbled_29_p1, rgbled_30_p1, rgbled_31_p1, rgbled_32_p1, rgbled_33_p1,
       rgbled_34_p1, rgbled_35_p1, rgbled_36_p1, rgbled_37_p1, rgbled_38_p1, rgbled_39_p1, rgbled_40_p1,
       rgbled_41_p1, rgbled_42_p1, rgbled_43_p1, rgbled_44_p1, rgbled_45_p1, rgbled_46_p1, rgbled_47_p1,
       rgbled_48_p1, rgbled_49_p1, rgbled_50_p1, rgbled_51_p1, rgbled_52_p1, rgbled_53_p1, rgbled_54_p1,
       rgbled_55_p1, rgbled_56_p1, rgbled_57_p1, rgbled_58_p1, rgbled_59_p1, rgbled_60_p1, rgbled_61_p1,
       rgbled_62_p1, rgbled_63_p1, rgbled_64_p1;
  wire [2:0] U_out;
  wire [4:0] Keypad, not_2_out;
  wire [7:0] D, demultiplexer_3_out0, demultiplexer_3_out1, demultiplexer_3_out2, demultiplexer_3_out3,
       multiplexer_2_out, register_1_q, xor_1_out;
  wire [9:0] and_1_out, and_2_out, and_3_out, and_4_out, and_5_out, multiplexer_1_out, P_out;

  Multiplexer #(.enable("false"), .width(10)) multiplexer_1 (
    .in0({P_out[9:6], U_out, N_out, P_out[0]}), .in1(10'h260), .out(multiplexer_1_out), .sel(rst_out));
  Button rst (.out(rst_out));
  LED led_1 (.in(Keypad[4]));
  Button Ctl (.out(P_out[6]));
  Button U (.out(U_out[0]));
  Button W (.out(P_out[7]));
  Button T (.out(U_out[1]));
  Button S (.out(P_out[8]));
  Button u_D (.out(U_out[2]));
  Button Alt (.out(P_out[9]));
  assign and_1_out = multiplexer_1_out & 10'h225;  // AND_Gate and_1, 10 bits wide
  assign and_2_out = multiplexer_1_out & 10'h312;  // AND_Gate and_2, 10 bits wide
  assign and_3_out = multiplexer_1_out & 10'h1a8;  // AND_Gate and_3, 10 bits wide
  assign and_4_out = multiplexer_1_out & 10'hd4;  // AND_Gate and_4, 10 bits wide
  assign and_5_out = multiplexer_1_out & 10'h4b;  // AND_Gate and_5, 10 bits wide
  Register register_1 (.D(D), .Q(register_1_q), .clk(clock_1_out));  // open: en, clr
  Clock clock_1 (.out(clock_1_out));
  LED led_2 (.in(Keypad[3]));
  LED led_3 (.in(Keypad[2]));
  Button N (.out(N_out[0]));
  Button E (.out(N_out[1]));
  Comparator #(.width(10)) comparator_1 (.a(and_1_out), .b({10{1'b0}}), .eq(Keypad[0]));  // open: gt, lt
  Comparator #(.width(10)) comparator_2 (.a(and_2_out), .b({10{1'b0}}), .eq(Keypad[1]));  // open: gt, lt
  Comparator #(.width(10)) comparator_3 (.a(and_3_out), .b({10{1'b0}}), .eq(Keypad[2]));  // open: gt, lt
  Comparator #(.width(10)) comparator_4 (.a(and_4_out), .b({10{1'b0}}), .eq(Keypad[3]));  // open: gt, lt
  Comparator #(.width(10)) comparator_5 (.a(and_5_out), .b({10{1'b0}}), .eq(Keypad[4]));  // open: gt, lt
  // NOT_Gate not_1 has open pins: in=in_1, out=open
  Multiplexer #(.enable("false"), .width(8)) multiplexer_2 (
    .in0(D), .in1(register_1_q), .out(multiplexer_2_out));  // open: sel
  assign not_2_out = ~Keypad;  // NOT_Gate not_2, 5 bits wide
  LED led_4 (.in(Keypad[1]));
  LED led_5 (.in(Keypad[0]));
  Button P (.out(P_out[0]));
  // Probe on {not_2_out[4:3], 1'b1, not_2_out[0], 1'b1, not_2_out[1], not_2_out[2], multiplexer_2_out}
  ROM #(.addrWidth(15)) LedCube (
    .addr({not_2_out[4:3], 1'b1, not_2_out[0], 1'b1, not_2_out[1], not_2_out[2], multiplexer_2_out}), .data(D));
  // RGBLED rgbled_1: pin names not known; wires that end beside it: rgbled_1_p1[0]
  // RGBLED rgbled_2: pin names not known; wires that end beside it: rgbled_2_p1[0]
  // RGBLED rgbled_3: pin names not known; wires that end beside it: rgbled_3_p1[0]
  // RGBLED rgbled_4: pin names not known; wires that end beside it: rgbled_4_p1[0]
  // RGBLED rgbled_5: pin names not known; wires that end beside it: rgbled_5_p1[0]
  // RGBLED rgbled_6: pin names not known; wires that end beside it: rgbled_6_p1[0]
  // RGBLED rgbled_7: pin names not known; wires that end beside it: rgbled_7_p1[0]
  // RGBLED rgbled_8: pin names not known; wires that end beside it: rgbled_8_p1[0]
  // RGBLED rgbled_9: pin names not known; wires that end beside it: rgbled_9_p1[0]
  // RGBLED rgbled_10: pin names not known; wires that end beside it: rgbled_10_p1[0]
  // RGBLED rgbled_11: pin names not known; wires that end beside it: rgbled_11_p1[0]
  // RGBLED rgbled_12: pin names not known; wires that end beside it: rgbled_12_p1[0]
  // RGBLED rgbled_13: pin names not known; wires that end beside it: rgbled_13_p1[0]
  // RGBLED rgbled_14: pin names not known; wires that end beside it: rgbled_14_p1[0]
  // RGBLED rgbled_15: pin names not known; wires that end beside it: rgbled_15_p1[0]
  // RGBLED rgbled_16: pin names not known; wires that end beside it: rgbled_16_p1[0]
  // RGBLED rgbled_17: pin names not known; wires that end beside it: rgbled_17_p1[0]
  // RGBLED rgbled_18: pin names not known; wires that end beside it: rgbled_18_p1[0]
  // RGBLED rgbled_19: pin names not known; wires that end beside it: rgbled_19_p1[0]
  // RGBLED rgbled_20: pin names not known; wires that end beside it: rgbled_20_p1[0]
  // RGBLED rgbled_21: pin names not known; wires that end beside it: rgbled_21_p1[0]
  // RGBLED rgbled_22: pin names not known; wires that end beside it: rgbled_22_p1[0]
  // RGBLED rgbled_23: pin names not known; wires that end beside it: rgbled_23_p1[0]
  // RGBLED rgbled_24: pin names not known; wires that end beside it: rgbled_24_p1[0]
  Multiplexer #(.enable("false")) multiplexer_3 (
    .in0(1'b1), .in1(clock_2_out), .out(multiplexer_3_out), .sel(xor_1_out[6]));
  Clock clock_2 (.out(clock_2_out));
  assign xor_1_out = D ^ 8'hf8;  // XOR_Gate xor_1, 8 bits wide
  // RGBLED rgbled_25: pin names not known; wires that end beside it: rgbled_25_p1[0]
  // RGBLED rgbled_26: pin names not known; wires that end beside it: rgbled_26_p1[0]
  // RGBLED rgbled_27: pin names not known; wires that end beside it: rgbled_27_p1[0]
  // RGBLED rgbled_28: pin names not known; wires that end beside it: rgbled_28_p1[0]
  // RGBLED rgbled_29: pin names not known; wires that end beside it: rgbled_29_p1[0]
  // RGBLED rgbled_30: pin names not known; wires that end beside it: rgbled_30_p1[0]
  // RGBLED rgbled_31: pin names not known; wires that end beside it: rgbled_31_p1[0]
  // RGBLED rgbled_32: pin names not known; wires that end beside it: rgbled_32_p1[0]
  // RGBLED rgbled_33: pin names not known; wires that end beside it: rgbled_33_p1[0]
  // RGBLED rgbled_34: pin names not known; wires that end beside it: rgbled_34_p1[0]
  // RGBLED rgbled_35: pin names not known; wires that end beside it: rgbled_35_p1[0]
  // RGBLED rgbled_36: pin names not known; wires that end beside it: rgbled_36_p1[0]
  // RGBLED rgbled_37: pin names not known; wires that end beside it: rgbled_37_p1[0]
  // RGBLED rgbled_38: pin names not known; wires that end beside it: rgbled_38_p1[0]
  // RGBLED rgbled_39: pin names not known; wires that end beside it: rgbled_39_p1[0]
  // RGBLED rgbled_40: pin names not known; wires that end beside it: rgbled_40_p1[0]
  Demultiplexer #(.enable("false")) demultiplexer_1 (
    .out0(demultiplexer_1_out0[0]), .out1(demultiplexer_1_out0[1]), .in(multiplexer_3_out), .sel(xor_1_out[7]));
  Demultiplexer #(.enable("false"), .select(2), .width(2)) demultiplexer_2 (
    .out0(demultiplexer_2_out0), .out1(demultiplexer_2_out1), .out2(demultiplexer_2_out2),
    .out3(demultiplexer_2_out3), .in(demultiplexer_1_out0), .sel({xor_1_out[3], xor_2_out[0]}));
  xor xor_2 (xor_2_out[0], xor_1_out[3], xor_1_out[0]);
  // Probe on D
  // RGBLED rgbled_41: pin names not known; wires that end beside it: rgbled_41_p1[0]
  // RGBLED rgbled_42: pin names not known; wires that end beside it: rgbled_42_p1[0]
  // RGBLED rgbled_43: pin names not known; wires that end beside it: rgbled_43_p1[0]
  // RGBLED rgbled_44: pin names not known; wires that end beside it: rgbled_44_p1[0]
  // RGBLED rgbled_45: pin names not known; wires that end beside it: rgbled_45_p1[0]
  // RGBLED rgbled_46: pin names not known; wires that end beside it: rgbled_46_p1[0]
  // RGBLED rgbled_47: pin names not known; wires that end beside it: rgbled_47_p1[0]
  // RGBLED rgbled_48: pin names not known; wires that end beside it: rgbled_48_p1[0]
  // RGBLED rgbled_49: pin names not known; wires that end beside it: rgbled_49_p1[0]
  // RGBLED rgbled_50: pin names not known; wires that end beside it: rgbled_50_p1[0]
  // RGBLED rgbled_51: pin names not known; wires that end beside it: rgbled_51_p1[0]
  // RGBLED rgbled_52: pin names not known; wires that end beside it: rgbled_52_p1[0]
  Demultiplexer #(.enable("false"), .select(2), .width(8)) demultiplexer_3 (
    .out0(demultiplexer_3_out0), .out1(demultiplexer_3_out1), .out2(demultiplexer_3_out2),
    .out3(demultiplexer_3_out3),
    .in({demultiplexer_2_out3, demultiplexer_2_out2, demultiplexer_2_out1, demultiplexer_2_out0}),
    .sel({xor_1_out[4], xor_3_out[0]}));
  xor xor_3 (xor_3_out[0], xor_1_out[4], xor_1_out[1]);
  // RGBLED rgbled_53: pin names not known; wires that end beside it: rgbled_53_p1[0]
  // RGBLED rgbled_54: pin names not known; wires that end beside it: rgbled_54_p1[0]
  // RGBLED rgbled_55: pin names not known; wires that end beside it: rgbled_55_p1[0]
  // RGBLED rgbled_56: pin names not known; wires that end beside it: rgbled_56_p1[0]
  // RGBLED rgbled_57: pin names not known; wires that end beside it: rgbled_57_p1[0]
  // RGBLED rgbled_58: pin names not known; wires that end beside it: rgbled_58_p1[0]
  // RGBLED rgbled_59: pin names not known; wires that end beside it: rgbled_59_p1[0]
  // RGBLED rgbled_60: pin names not known; wires that end beside it: rgbled_60_p1[0]
  // RGBLED rgbled_61: pin names not known; wires that end beside it: rgbled_61_p1[0]
  // RGBLED rgbled_62: pin names not known; wires that end beside it: rgbled_62_p1[0]
  // RGBLED rgbled_63: pin names not known; wires that end beside it: rgbled_63_p1[0]
  // RGBLED rgbled_64: pin names not known; wires that end beside it: rgbled_64_p1[0]
  Demultiplexer #(.enable("false"), .select(2), .width(32)) demultiplexer_4 (
    .out0({rgbled_2_p1, rgbled_12_p1, rgbled_28_p1, rgbled_43_p1, rgbled_1_p1, rgbled_11_p1, rgbled_27_p1, rgbled_55_p1, rgbled_10_p1, rgbled_26_p1, rgbled_42_p1, rgbled_54_p1, rgbled_9_p1, rgbled_25_p1, rgbled_41_p1, rgbled_53_p1}),
    .out1({rgbled_4_p1, rgbled_16_p1, rgbled_32_p1, rgbled_46_p1, rgbled_3_p1, rgbled_15_p1, rgbled_31_p1, rgbled_58_p1, rgbled_14_p1, rgbled_30_p1, rgbled_45_p1, rgbled_57_p1, rgbled_13_p1, rgbled_29_p1, rgbled_44_p1, rgbled_56_p1}),
    .out2({rgbled_6_p1, rgbled_20_p1, rgbled_36_p1, rgbled_49_p1, rgbled_5_p1, rgbled_19_p1, rgbled_35_p1, rgbled_61_p1, rgbled_18_p1, rgbled_34_p1, rgbled_48_p1, rgbled_60_p1, rgbled_17_p1, rgbled_33_p1, rgbled_47_p1, rgbled_59_p1}),
    .out3({rgbled_8_p1, rgbled_24_p1, rgbled_40_p1, rgbled_52_p1, rgbled_7_p1, rgbled_23_p1, rgbled_39_p1, rgbled_64_p1, rgbled_22_p1, rgbled_38_p1, rgbled_51_p1, rgbled_63_p1, rgbled_21_p1, rgbled_37_p1, rgbled_50_p1, rgbled_62_p1}),
    .in({demultiplexer_3_out3, demultiplexer_3_out2, demultiplexer_3_out1, demultiplexer_3_out0}),
    .sel({xor_1_out[5], xor_4_out[0]}));
  xor xor_4 (xor_4_out[0], xor_1_out[5], xor_1_out[2]);

  // Other names for the same wires on the sheet: latch_bpass = in_1

  // Notes on the sheet:
  //   contents of LedCube (hex, n*v repeats v):
  //   0 81 82 3 84 5 6 87 88 9 a 8b c 8d 8e f 90 11 12 93 14 95 96 17 18 99 9a 1b 9c 1d 1e 9f a0 21 22 a3
  //   24 a5 a6 27 28 a9 aa 2b ac 2d 2e af 30 b1 b2 33 b4 35 36 b7 b8 39 3a bb 3c bd be 3f c0 41 42 c3 44
  //   c5 c6 47 48 c9 ca 4b cc 4d 4e cf 50 d1 d2 53 d4 55 56 d7 d8 59 5a db 5c dd de 5f 60 e1 e2 63 e4 65
  //   66 e7 e8 69 6a eb 6c ed ee 6f f0 71 72 f3 74 f5 f6 77 78 f9 fa 7b fc 7d 7e ff 0 81 82 3 84 5 6 87 88
  //   9 a 8b c 8d 8e f 90 11 12 93 14 95 96 17 18 99 9a 1b 9c 1d 1e 9f a0 21 22 a3 24 a5 a6 27 28 a9 aa 2b
  //   ac 2d 2e af 30 b1 b2 33 b4 35 36 b7 b8 39 3a bb 3c bd be 3f c0 41 42 c3 44 c5 c6 47 48 c9 ca 4b cc
  //   4d 4e cf 50 d1 d2 53 d4 55 56 d7 d8 59 5a db 5c dd de 5f 60 e1 e2 63 e4 65 66 e7 e8 69 6a eb 6c ed
  //   ee 6f f0 71 72 f3 74 f5 f6 77 78 f9 fa 7b fc 7d 7e ff 0 1 2 3 4 5 6 7 8 9 a b c d e f 10 11 12 13 14
  //   15 16 17 18 19 1a 1b 1c 1d 1e 1f 20 21 22 23 24 25 26 27 28 29 2a 2b 2c 2d 2e 2f 30 31 32 33 34 35
  //   36 37 38 39 3a 3b 3c 3d 3e 3f 40 41 42 43 44 45 46 47 48 49 4a 4b 4c 4d 4e 4f 50 51 52 53 54 55 56
  //   57 58 59 5a 5b 5c 5d 5e 5f 60 61 62 63 64 65 66 67 68 69 6a 6b 6c 6d 6e 6f 70 71 72 73 74 75 76 77
  //   78 79 7a 7b 7c 7d 7e 7f 80 81 82 83 84 85 86 87 88 89 8a 8b 8c 8d 8e 8f 90 91 92 93 94 95 96 97 98
  //   99 9a 9b 9c 9d 9e 9f a0 a1 a2 a3 a4 a5 a6 a7 a8 a9 aa ab ac ad ae af b0 b1 b2 b3 b4 b5 b6 b7 b8 b9
  //   ba bb bc bd be bf c0 c1 c2 c3 c4 c5 c6 c7 c8 c9 ca cb cc cd ce cf d0 d1 d2 d3 d4 d5 d6 d7 d8 d9 da
  //   db dc dd de df e0 e1 e2 e3 e4 e5 e6 e7 e8 e9 ea eb ec ed ee ef f0 f1 f2 f3 f4 f5 f6 f7 f8 f9 fa fb
  //   fc fd fe ff 0 1 2 3 4 5 6 7 8 9 a b c d e f 10 11 12 13 14 15 16 17 18 19 1a 1b 1c 1d 1e 1f 20 21 22
  //   23 24 25 26 27 28 29 2a 2b 2c 2d 2e 2f 30 31 32 33 34 35 36 37 38 39 3a 3b 3c 3d 3e 3f 40 41 42 43
  //   44 45 46 47 48 49 4a 4b 4c 4d 4e 4f 50 51 52 53 54 55 56 57 58 59 5a 5b 5c 5d 5e 5f 60 61 62 63 64
  //   65 66 67 68 69 6a 6b 6c 6d 6e 6f 70 71 72 73 74 75 76 77 78 79 7a 7b 7c 7d 7e 7f 80 81 82 83 84 85
  //   86 87 88 89 8a 8b 8c 8d 8e 8f 90 91 92 93 94 95 96 97 98 99 9a 9b 9c 9d 9e 9f a0 a1 a2 a3 a4 a5 a6
  //   a7 a8 a9 aa ab ac ad ae af b0 b1 b2 b3 b4 b5 b6 b7 b8 b9 ba bb bc bd be bf c0 c1 c2 c3 c4 c5 c6 c7
  //   c8 c9 ca cb cc cd ce cf d0 d1 d2 d3 d4 d5 d6 d7 d8 d9 da db dc dd de df e0 e1 e2 e3 e4 e5 e6 e7 e8
  //   e9 ea eb ec ed ee ef f0 f1 f2 f3 f4 f5 f6 f7 f8 f9 fa fb fc fd fe ff 10 1 2 1 4 15 4 7 8 19 8 b 1c d
  //   e d 10 13 2 13 16 15 16 7 1a 19 1a b 1c 1f e 1f 20 31 20 23 34 25 26 25 38 29 2a 29 2c 3d 2c 2f 32
  //   31 32 23 34 37 26 37 38 3b 2a 3b 3e 3d 3e 2f 40 51 40 43 54 45 46 45 58 49 4a 49 4c 5d 4c 4f 52 51
  //   52 43 54 57 46 57 58 5b 4a 5b 5e 5d 5e 4f 70 61 62 61 64 75 64 67 68 79 68 6b 7c 6d 6e 6d 70 73 62
  //   73 76 75 76 67 7a 79 7a 6b 7c 7f 6e 7f 80 91 80 83 94 85 86 85 98 89 8a 89 8c 9d 8c 8f 92 91 92 83
  //   94 97 86 97 98 9b 8a 9b 9e 9d 9e 8f b0 a1 a2 a1 a4 b5 a4 a7 a8 b9 a8 ab bc ad ae ad b0 b3 a2 b3 b6
  //   b5 b6 a7 ba b9 ba ab bc bf ae bf d0 c1 c2 c1 c4 d5 c4 c7 c8 d9 c8 cb dc cd ce cd d0 d3 c2 d3 d6 d5
  //   d6 c7 da d9 da cb dc df ce df e0 f1 e0 e3 f4 e5 e6 e5 f8 e9 ea e9 ec fd ec ef f2 f1 f2 e3 f4 f7 e6
  //   f7 f8 fb ea fb fe fd fe ef 1024*ff 0 1 2 3 4 5 6 7 8 9 a b c d e f 10 11 12 13 14 15 16 17 18 19 1a
  //   1b 1c 1d 1e 1f 20 21 22 23 24 25 26 27 28 29 2a 2b 2c 2d 2e 2f 30 31 32 33 34 35 36 37 38 39 3a 3b
  //   3c 3d 3e 3f 40 41 42 43 44 45 46 47 48 49 4a 4b 4c 4d 4e 4f 50 51 52 53 54 55 56 57 58 59 5a 5b 5c
  //   5d 5e 5f 60 61 62 63 64 65 66 67 68 69 6a 6b 6c 6d 6e 6f 70 71 72 73 74 75 76 77 78 79 7a 7b 7c 7d
  //   7e 7f 80 81 82 83 84 85 86 87 88 89 8a 8b 8c 8d 8e 8f 90 91 92 93 94 95 96 97 98 99 9a 9b 9c 9d 9e
  //   9f a0 a1 a2 a3 a4 a5 a6 a7 a8 a9 aa ab ac ad ae af b0 b1 b2 b3 b4 b5 b6 b7 b8 b9 ba bb bc bd be bf
  //   c0 c1 c2 c3 c4 c5 c6 c7 c8 c9 ca cb cc cd ce cf d0 d1 d2 d3 d4 d5 d6 d7 d8 d9 da db dc dd de df e0
  //   e1 e2 e3 e4 e5 e6 e7 e8 e9 ea eb ec ed ee ef f0 f1 f2 f3 f4 f5 f6 f7 f8 f9 fa fb fc fd fe ff 20 1 2
  //   23 4 1 2 7 8 29 2a b 8 d e b 10 31 32 13 10 15 16 13 38 19 1a 3b 1c 19 1a 1f 20 25 26 23 4 25 26 7
  //   2c 29 2a 2f 2c d e 2f 34 31 32 37 34 15 16 37 38 3d 3e 3b 1c 3d 3e 1f 40 61 62 43 40 45 46 43 68 49
  //   4a 6b 4c 49 4a 4f 70 51 52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
endmodule
